# Fritzing sketch pcbv1 (saved by Fritzing 0.9.0b)
circuit board: 2.62004cm x 3.09059cm
breadboards: 1

parts:
  ISP1 = double row female pin header, 6 pins [form="♀ (female)"]
  U8 = ATmega328 [package=tqfp]
  R2 = Resistor [tolerance=±5% resistance=10k package="0805 [SMD]"]
  J1 = Generic double row female header - 8 pins [form="♀ (female)" package=THT]
  BAT1 = Battery Holders [package=battcom_20mm_pth]
  C5 = Tantalum Capacitor [capacitance=47µF package="C 6032 [SMD, tantalum]"]
  C4 = Tantalum Capacitor [capacitance=47µF package="D 7343 [SMD, tantalum]"]

nets:
  N1: ISP1.pin1, U8.PB4(MISO), J1.miso
  N2: ISP1.pin2, U8.PB5(SCK), J1.sck
  N3: ISP1.pin3, U8.PC6(_RESET), R2.Pin_0
  GND: ISP1.pin4, U8.GND, J1.gnd, BAT1.-, C5.-, C4.-
  N4: ISP1.pin5, U8.PB3(MOSI_OC2), J1.mosi
  VCC: ISP1.pin6, U8.VCC, R2.Pin_1, J1.vcc, BAT1.+, C5.+, C4.+
  N5: U8.PD3(INT1), J1.irq
  N6: U8.PD5(T1), J1.ce
  N7: U8.PD6(AIN0), J1.csn

custom parts:
  Generic double row female header - 8 pins: Generic double row female header
